// Logisim project RiskV.circ as structural Verilog: 10 circuits, main circuit ProgramCounter
module ProgramCounter (
  input  [31:0] TargetAddr,
  input  BranchCtl,
  input  Clk,
  input  Reset,
  output [31:0] PcOut,
  output [31:0] PcPlus4
);

  wire [31:0] multiplexer_1_out;

  Multiplexer #(.width(32)) multiplexer_1 (.in0(PcPlus4), .in1(TargetAddr), .out(multiplexer_1_out), .sel(BranchCtl));
  Register #(.width(32)) register_1 (.D(multiplexer_1_out), .en(1'b1), .clk(Clk), .Q(PcOut), .clr(Reset));
  Adder #(.width(32)) adder_1 (.a(32'h4), .b(PcOut), .out(PcPlus4));  // open: cin, cout
endmodule

module RegisterFile (
  input  [31:0] Data,
  input  [4:0] RdAddr,
  input  [4:0] Rs1Addr,
  input  [4:0] Rs2Addr,
  input  WriteEnable,
  input  Clk,
  output [31:0] Rs1Out,
  output [31:0] Rs2Out
);

  wire clk_t, x1_we, x2_we, x3_we, x4_we, x5_we, x6_we, x7_we, x8_we, x9_we, x10_we, x11_we, x12_we, x13_we,
       x14_we, x15_we, x16_we, x17_we, x18_we, x19_we, x20_we, x21_we, x22_we, x23_we, x24_we, x25_we,
       x26_we, x27_we, x28_we, x29_we, x30_we, x31_we;
  wire [31:0] x1, x2, x3, x4, x5, x6, x7, x8, x9, x10, x11, x12, x13, x14, x15, x16, x17, x18, x19, x20, x21,
       x22, x23, x24, x25, x26, x27, x28, x29, x30, x31;

  Clock clock_1 (.out(clk_t));
  Demultiplexer #(.select(5)) demultiplexer_1 (
    .out1(x1_we), .out2(x2_we), .out3(x3_we), .out4(x4_we), .out5(x5_we), .out6(x6_we), .out7(x7_we),
    .out8(x8_we), .out9(x9_we), .out10(x10_we), .out11(x11_we), .out12(x12_we), .out13(x13_we),
    .out14(x14_we), .out15(x15_we), .out16(x16_we), .out17(x17_we), .out18(x18_we), .out19(x19_we),
    .out20(x20_we), .out21(x21_we), .out22(x22_we), .out23(x23_we), .out24(x24_we), .out25(x25_we),
    .out26(x26_we), .out27(x27_we), .out28(x28_we), .out29(x29_we), .out30(x30_we), .out31(x31_we),
    .in(WriteEnable), .sel(RdAddr));  // open: out0
  Register #(.width(32)) register_1 (.D(Data), .en(x1_we), .clk(clk_t), .Q(x1));  // open: clr
  Register #(.width(32)) register_2 (.D(Data), .en(x2_we), .clk(clk_t), .Q(x2));  // open: clr
  Register #(.width(32)) register_3 (.D(Data), .en(x3_we), .clk(clk_t), .Q(x3));  // open: clr
  Register #(.width(32)) register_4 (.D(Data), .en(x4_we), .clk(clk_t), .Q(x4));  // open: clr
  Register #(.width(32)) register_5 (.D(Data), .en(x5_we), .clk(clk_t), .Q(x5));  // open: clr
  Register #(.width(32)) register_6 (.D(Data), .en(x6_we), .clk(clk_t), .Q(x6));  // open: clr
  Register #(.width(32)) register_7 (.D(Data), .en(x7_we), .clk(clk_t), .Q(x7));  // open: clr
  Register #(.width(32)) register_8 (.D(Data), .en(x8_we), .clk(clk_t), .Q(x8));  // open: clr
  Register #(.width(32)) register_9 (.D(Data), .en(x9_we), .clk(clk_t), .Q(x9));  // open: clr
  Register #(.width(32)) register_10 (.D(Data), .en(x10_we), .clk(clk_t), .Q(x10));  // open: clr
  Register #(.width(32)) register_11 (.D(Data), .en(x11_we), .clk(clk_t), .Q(x11));  // open: clr
  Register #(.width(32)) register_12 (.D(Data), .en(x12_we), .clk(clk_t), .Q(x12));  // open: clr
  Register #(.width(32)) register_13 (.D(Data), .en(x13_we), .clk(clk_t), .Q(x13));  // open: clr
  Register #(.width(32)) register_14 (.D(Data), .en(x14_we), .clk(clk_t), .Q(x14));  // open: clr
  Register #(.width(32)) register_15 (.D(Data), .en(x15_we), .clk(clk_t), .Q(x15));  // open: clr
  Register #(.width(32)) register_16 (.D(Data), .en(x16_we), .clk(clk_t), .Q(x16));  // open: clr
  Register #(.width(32)) register_17 (.D(Data), .en(x17_we), .clk(clk_t), .Q(x17));  // open: clr
  Register #(.width(32)) register_18 (.D(Data), .en(x18_we), .clk(clk_t), .Q(x18));  // open: clr
  Register #(.width(32)) register_19 (.D(Data), .en(x19_we), .clk(clk_t), .Q(x19));  // open: clr
  Register #(.width(32)) register_20 (.D(Data), .en(x20_we), .clk(clk_t), .Q(x20));  // open: clr
  Register #(.width(32)) register_21 (.D(Data), .en(x21_we), .clk(clk_t), .Q(x21));  // open: clr
  Register #(.width(32)) register_22 (.D(Data), .en(x22_we), .clk(clk_t), .Q(x22));  // open: clr
  Register #(.width(32)) register_23 (.D(Data), .en(x23_we), .clk(clk_t), .Q(x23));  // open: clr
  Register #(.width(32)) register_24 (.D(Data), .en(x24_we), .clk(clk_t), .Q(x24));  // open: clr
  Register #(.width(32)) register_25 (.D(Data), .en(x25_we), .clk(clk_t), .Q(x25));  // open: clr
  Register #(.width(32)) register_26 (.D(Data), .en(x26_we), .clk(clk_t), .Q(x26));  // open: clr
  Register #(.width(32)) register_27 (.D(Data), .en(x27_we), .clk(clk_t), .Q(x27));  // open: clr
  Register #(.width(32)) register_28 (.D(Data), .en(x28_we), .clk(clk_t), .Q(x28));  // open: clr
  Register #(.width(32)) register_29 (.D(Data), .en(x29_we), .clk(clk_t), .Q(x29));  // open: clr
  Register #(.width(32)) register_30 (.D(Data), .en(x30_we), .clk(clk_t), .Q(x30));  // open: clr
  Register #(.width(32)) register_31 (.D(Data), .en(x31_we), .clk(clk_t), .Q(x31));  // open: clr
  Multiplexer #(.select(5), .width(32)) multiplexer_1 (
    .in0({32{1'b0}}), .in1(x1), .in2(x2), .in3(x3), .in4(x4), .in5(x5), .in6(x6), .in7(x7), .in8(x8),
    .in9(x9), .in10(x10), .in11(x11), .in12(x12), .in13(x13), .in14(x14), .in15(x15), .in16(x16), .in17(x17),
    .in18(x18), .in19(x19), .in20(x20), .in21(x21), .in22(x22), .in23(x23), .in24(x24), .in25(x25),
    .in26(x26), .in27(x27), .in28(x28), .in29(x29), .in30(x30), .in31(x31), .out(Rs1Out), .sel(Rs1Addr));
  Multiplexer #(.select(5), .width(32)) multiplexer_2 (
    .in0({32{1'b0}}), .in1(x1), .in2(x2), .in3(x3), .in4(x4), .in5(x5), .in6(x6), .in7(x7), .in8(x8),
    .in9(x9), .in10(x10), .in11(x11), .in12(x12), .in13(x13), .in14(x14), .in15(x15), .in16(x16), .in17(x17),
    .in18(x18), .in19(x19), .in20(x20), .in21(x21), .in22(x22), .in23(x23), .in24(x24), .in25(x25),
    .in26(x26), .in27(x27), .in28(x28), .in29(x29), .in30(x30), .in31(x31), .out(Rs2Out), .sel(Rs2Addr));

  // Other names for the same wires on the sheet: rd[4:0] = RdAddr; rs1[4:0] = Rs1Addr; rs2[4:0] = Rs2Addr;
  //   we_in = WriteEnable
endmodule

module MainControlDecoder (
  input  [31:0] Inst,
  input  BranchTaken,
  output [2:0] ImmSel,
  output ASel,
  output BSel,
  output [3:0] ALUSel,
  output [2:0] BrSel,
  output PCSel,
  output MemRead,
  output MemWrite,
  output RegWEn,
  output [1:0] WBSel,
  output Is_Ecall,
  output Is_Ebreak
);

  wire and_1_out, and_15_out, AUIPC, Branch, I_Type, JALR, LUI, nand_1_out, not_1_out, or_2_out, or_4_out,
       or_6_out, or_7_out, R_Type, System;

  nand nand_1 (nand_1_out, Inst[12], Inst[13], Inst[14]);
  and and_1 (and_1_out, System, nand_1_out);
  and and_2 (Is_Ebreak, Inst[20], and_1_out);
  and and_3 (Is_Ecall, and_1_out, not_1_out);
  not not_1 (not_1_out, Inst[20]);
  and and_4 (R_Type, Inst[0], Inst[1], ~Inst[2], ~Inst[3], Inst[4], Inst[5], ~Inst[6]);  // AND_Gate
  and and_5 (I_Type, Inst[0], Inst[1], ~Inst[2], ~Inst[3], Inst[4], ~Inst[5], ~Inst[6]);  // AND_Gate
  and and_6 (MemRead, Inst[0], Inst[1], ~Inst[2], ~Inst[3], ~Inst[4], ~Inst[5], ~Inst[6]);  // AND_Gate
  and and_7 (MemWrite, Inst[0], Inst[1], ~Inst[2], ~Inst[3], ~Inst[4], Inst[5], ~Inst[6]);  // AND_Gate
  and and_8 (ImmSel[2], Inst[0], Inst[1], Inst[2], Inst[3], ~Inst[4], Inst[5], Inst[6]);  // AND_Gate
  and and_9 (Branch, Inst[0], Inst[1], ~Inst[2], ~Inst[3], ~Inst[4], Inst[5], Inst[6]);  // AND_Gate
  and and_10 (AUIPC, Inst[0], Inst[1], Inst[2], ~Inst[3], Inst[4], ~Inst[5], ~Inst[6]);  // AND_Gate
  and and_11 (LUI, Inst[0], Inst[1], Inst[2], ~Inst[3], Inst[4], Inst[5], ~Inst[6]);  // AND_Gate
  and and_12 (System, Inst[0], Inst[1], ~Inst[2], ~Inst[3], Inst[4], Inst[5], Inst[6]);  // AND_Gate
  and and_13 (JALR, Inst[0], Inst[1], Inst[2], ~Inst[3], ~Inst[4], Inst[5], Inst[6]);  // AND_Gate
  or or_1 (WBSel[1], ImmSel[2], JALR);
  or or_2 (or_2_out, LUI, AUIPC);
  or or_3 (ImmSel[1], or_2_out, Branch);
  or or_4 (or_4_out, MemWrite, Branch);
  not not_2 (RegWEn, or_4_out);
  or or_5 (ImmSel[0], or_2_out, MemWrite);
  or or_6 (or_6_out, I_Type, R_Type);
  and and_14 (ALUSel[0], or_6_out, Inst[30]);
  or or_7 (or_7_out, ImmSel[2], JALR);
  and and_15 (and_15_out, BranchTaken, Branch);
  or or_8 (ASel, AUIPC, ImmSel[2], Branch);
  or or_9 (BSel, MemWrite, MemRead, I_Type, AUIPC, ImmSel[2], JALR);
  or or_10 (PCSel, or_7_out, and_15_out);

  assign ALUSel[3:1] = Inst[14:12];
  assign BrSel = Inst[14:12];
  assign WBSel[0] = MemRead;

  // Other names for the same wires on the sheet: func3[2:0] = Inst[14:12]; branch_taken = BranchTaken;
  //   ebreak = Is_Ebreak; ecall = Is_Ecall; JAL = ImmSel[2]; op_code[6:0] = Inst[6:0]; func7[6:0] = Inst[31:25];
  //   Store = MemWrite; Load = MemRead

  // Notes on the sheet:
  //   Funct3 == 000
  //   SYSTEM_CTL
  //   R_TYPE == 011 0011
  //   I_Type == 001 0011
  //   Load == 000 0011
  //   Store == 010 0011
  //   JAL == 110 1111
  //   Branch == 110 0011
  //   AUIPC == 001 0111
  //   LUI == 011 0111
  //   SYSTEM == 1110011
  //   JALR == 110 0111
  //   MEM_Control
  //   WB_Control
  //   Trap_Control
  //   ID_Control
  //   EX_Control
  //   (1 bit): Breakpoint trap flag.
  //   (1 bit): Enables Data Memory read operations.
  //   (1 bit): Enables Data Memory write operations.
  //   (1 bit): Selects the writeback source (ALU result vs. Memory read data).
  //   (3bit):  Send to ImmGen Sel input
  //   ImmSel[0] = Store OR LUI OR AUIPC
  //   ImmSel[1] = Branch OR LUI OR AUIPC
  //   ImmSel[2] = JAL
  //   (1 bit): Selects ALU operand A
  //   ASel = AUIPC OR Branch OR JAL
  //   ALUSel[1] = funct3[0]
  //   ALUSel[2] = funct3[1]
  //   ALUSel[3] = funct3[2]
  //   (1 bit): Master write-enable for the register file.
  //   (2 bit): Selects the writeback source (ALU result vs. Memory read data).
  //   (1 bit): Selects ALU operand B (Register vs. Immediate).
  //   BSel = IType OR Load OR Store OR AUIPC OR JAL OR JALR
  //   ALUSel[0] = funct7[5] AND (RType OR IType)
  //   (3bit): 3 Bit branch selector code sent directly to the BranchControl
  //   (1 bit): Signals a conditional branch instruction to the Branch Selector.
  //   (4 bits): Sent directly to ALUSel bus Top 3 bits from funct3 LSB from funct7[5]
endmodule

module BranchControl (
  input  [31:0] dataA,
  input  [31:0] dataB,
  input  [2:0] BrSel,
  output TakeBranch
);

  wire subtractor_1_bout, wordlevelcomparator_1_eq, wordlevelcomparator_1_lts, wordlevelcomparator_1_ltu;
  wire [31:0] subtractor_1_out;

  Subtractor #(.width(32)) subtractor_1 (
    .a(dataA), .b(dataB), .out(subtractor_1_out), .bout(subtractor_1_bout));  // open: bin
  WordLevelComparator wordlevelcomparator_1 (
    .InSum(subtractor_1_out), .InCout(subtractor_1_bout), .ASignIn(dataA[31]), .BSignIn(dataB[31]),
    .EQ(wordlevelcomparator_1_eq), .LTU(wordlevelcomparator_1_ltu), .LTS(wordlevelcomparator_1_lts));
  BranchSelector branchselector_1 (
    .EQ(wordlevelcomparator_1_eq), .LTS(wordlevelcomparator_1_lts), .LTU(wordlevelcomparator_1_ltu),
    .func3(BrSel), .TakeBranch(TakeBranch));

  // Other names for the same wires on the sheet: ASign = dataA[31]; BSign = dataB[31]
endmodule

module WordLevelComparator (
  input  [31:0] InSum,
  input  InCout,
  input  ASignIn,
  input  BSignIn,
  output EQ,
  output LTU,
  output LTS
);

  wire or_1_out, xor_1_out;

  not not_1 (LTU, InCout);
  xor xor_1 (xor_1_out, ASignIn, BSignIn);
  Multiplexer multiplexer_1 (.in0(LTU), .in1(ASignIn), .out(LTS), .sel(xor_1_out));
  or or_1 (or_1_out, InSum[0], InSum[1], InSum[2], InSum[3], InSum[4], InSum[5], InSum[6], InSum[7], InSum[8], InSum[9], InSum[10], InSum[11], InSum[12], InSum[13], InSum[14], InSum[15], InSum[16], InSum[17], InSum[18], InSum[19], InSum[20], InSum[21], InSum[22], InSum[23], InSum[24], InSum[25], InSum[26], InSum[27], InSum[28], InSum[29], InSum[30], InSum[31]);
  not not_2 (EQ, or_1_out);
endmodule

module BranchSelector (
  input  EQ,
  input  LTS,
  input  LTU,
  input  [2:0] func3,
  output TakeBranch
);

  wire not_1_out, not_2_out, not_3_out;

  not not_1 (not_1_out, EQ);
  not not_2 (not_2_out, LTS);
  not not_3 (not_3_out, LTU);
  Multiplexer #(.select(3)) multiplexer_1 (
    .in0(EQ), .in1(not_1_out), .in2(1'b0), .in3(1'b0), .in4(LTS), .in5(not_2_out), .in6(LTU),
    .in7(not_3_out), .out(TakeBranch), .sel(func3));
endmodule

module BitwiseLogicUnit (
  input  [31:0] B,
  input  [31:0] A,
  input  [2:0] func3,
  output [31:0] Out0
);

  wire [31:0] and_1_out, or_1_out, xor_1_out;

  assign xor_1_out = A ^ B;  // XOR_Gate xor_1, 32 bits wide
  assign or_1_out = B | A;  // OR_Gate or_1, 32 bits wide
  assign and_1_out = B & A;  // AND_Gate and_1, 32 bits wide
  Multiplexer #(.select(2), .width(32)) multiplexer_1 (
    .in0(xor_1_out), .in1({32{1'b0}}), .in2(or_1_out), .in3(and_1_out), .out(Out0), .sel(func3[1:0]));
endmodule

module ImmGen32Bit (
  input  [31:0] InstIn,
  input  [2:0] ImmSelIn,
  output [31:0] ImmOut
);

  Multiplexer #(.select(3), .width(32)) multiplexer_1 (
    .in0({{21{InstIn[31]}}, InstIn[30:20]}), .in1({{21{InstIn[31]}}, InstIn[30:25], InstIn[11:7]}),
    .in2({{20{InstIn[31]}}, InstIn[7], InstIn[30:25], InstIn[11:8], 1'b0}),
    .in3({InstIn[31:12], {12{1'b0}}}),
    .in4({{12{InstIn[31]}}, InstIn[19:12], InstIn[20], InstIn[30:21], 1'b0}), .out(ImmOut), .sel(ImmSelIn));  // open: in5, in6, in7

  // Other names for the same wires on the sheet: BType[31:1] = {{20{InstIn[31]}}, InstIn[7], InstIn[30:25], InstIn[11:8]};
  //   Ins8 = InstIn[8]; SType[31:0] = {{21{InstIn[31]}}, InstIn[30:25], InstIn[11:7]}; Ins9 = InstIn[9];
  //   Ins10 = InstIn[10]; Ins11 = InstIn[11]; Ins7 = InstIn[7]; ImmSel[2:0] = ImmSelIn; Ins0 = InstIn[0];
  //   Ins1 = InstIn[1]; Ins2 = InstIn[2]; Ins3 = InstIn[3]; Ins4 = InstIn[4]; Ins5 = InstIn[5]; Ins6 = InstIn[6];
  //   Ins21 = InstIn[21]; IType[31:0] = {{21{InstIn[31]}}, InstIn[30:20]};
  //   JType[31:1] = {{12{InstIn[31]}}, InstIn[19:12], InstIn[20], InstIn[30:21]}; UType[31:12] = InstIn[31:12];
  //   Ins22 = InstIn[22]; Ins23 = InstIn[23]; Ins24 = InstIn[24]; Ins25 = InstIn[25]; Ins26 = InstIn[26];
  //   Ins27 = InstIn[27]; Ins28 = InstIn[28]; Ins29 = InstIn[29]; Ins30 = InstIn[30]; Ins20 = InstIn[20];
  //   Ins12 = InstIn[12]; Ins13 = InstIn[13]; Ins14 = InstIn[14]; Ins15 = InstIn[15]; Ins16 = InstIn[16];
  //   Ins17 = InstIn[17]; Ins18 = InstIn[18]; Ins19 = InstIn[19]; Ins31 = InstIn[31]

  // Notes on the sheet:
  //   I-Type
  //   S-Type
  //   B-Type
  //   U-Type
  //   J-Type
endmodule

module ImmGen64Bit (
  input  [31:0] InstIn,
  input  [2:0] ImmSelIn,
  output [63:0] ImmOut
);

  Multiplexer #(.select(3), .width(64)) multiplexer_1 (
    .in0({{53{InstIn[31]}}, InstIn[30:20]}), .in1({{53{InstIn[31]}}, InstIn[30:25], InstIn[11:7]}),
    .in2({{52{InstIn[31]}}, InstIn[7], InstIn[30:25], InstIn[11:8], 1'b0}),
    .in3({{33{InstIn[31]}}, InstIn[30:12], {12{1'b0}}}),
    .in4({{44{InstIn[31]}}, InstIn[19:12], InstIn[20], InstIn[30:21], 1'b0}), .out(ImmOut), .sel(ImmSelIn));  // open: in5, in6, in7

  // Other names for the same wires on the sheet: BType[63:1] = {{52{InstIn[31]}}, InstIn[7], InstIn[30:25], InstIn[11:8]};
  //   Ins8 = InstIn[8]; SType[63:0] = {{53{InstIn[31]}}, InstIn[30:25], InstIn[11:7]}; Ins9 = InstIn[9];
  //   Ins10 = InstIn[10]; Ins11 = InstIn[11]; Ins7 = InstIn[7]; ImmSel[2:0] = ImmSelIn; Ins0 = InstIn[0];
  //   Ins1 = InstIn[1]; Ins2 = InstIn[2]; Ins3 = InstIn[3]; Ins4 = InstIn[4]; Ins5 = InstIn[5]; Ins6 = InstIn[6];
  //   Ins21 = InstIn[21]; IType[63:0] = {{53{InstIn[31]}}, InstIn[30:20]};
  //   JType[63:1] = {{44{InstIn[31]}}, InstIn[19:12], InstIn[20], InstIn[30:21]};
  //   UType[63:12] = {{33{InstIn[31]}}, InstIn[30:12]}; Ins22 = InstIn[22]; Ins23 = InstIn[23]; Ins24 = InstIn[24];
  //   Ins25 = InstIn[25]; Ins26 = InstIn[26]; Ins27 = InstIn[27]; Ins28 = InstIn[28]; Ins29 = InstIn[29];
  //   Ins30 = InstIn[30]; Ins20 = InstIn[20]; Ins12 = InstIn[12]; Ins13 = InstIn[13]; Ins14 = InstIn[14];
  //   Ins15 = InstIn[15]; Ins16 = InstIn[16]; Ins17 = InstIn[17]; Ins18 = InstIn[18]; Ins19 = InstIn[19];
  //   Ins31 = InstIn[31]

  // Notes on the sheet:
  //   I-Type
  //   S-Type
  //   B-Type
  //   U-Type
  //   J-Type
endmodule

module RiskVCPUSingleCycle (
);

  BranchControl branchcontrol_1 ();  // open: dataA, dataB, BrSel, TakeBranch
  MainControlDecoder maincontroldecoder_1 ();  // open: Inst, BranchTaken, ImmSel, ASel, BSel, ALUSel, BrSel, PCSel, MemRead, MemWrite, RegWEn, WBSel, Is_Ecall, Is_Ebreak
  ProgramCounter programcounter_1 ();  // open: TargetAddr, BranchCtl, Clk, Reset, PcOut, PcPlus4
endmodule
